// Logisim project CPU.circ as structural Verilog: 7 circuits, main circuit main
module main (
);

  wire and_1_out, and_2_out, branch_or_jump_out, clock_1_out, controlu_1_alusrc, controlu_1_branch,
       controlu_1_jump, controlu_1_jumpback, controlu_1_memread, controlu_1_memtoreq, controlu_1_memwrite,
       controlu_1_regdst, controlu_1_regwrite, or_1_out;
  wire [3:0] controlu_1_aluop1;
  wire [4:0] multiplexer_3_out;
  wire [15:0] alu_1_out, multiplexer_1_out, multiplexer_2_out, multiplexer_4_out, multiplexer_5_out,
       n16bit_adder_1_sum, PC_q, ram_1_data, ram_2_data, register_1_q, register_file_1_r1, register_file_1_r2;
  wire [31:16] ram_1_data_2;

  Register #(.width(16)) register_1 (
    .D(n16bit_adder_1_sum), .en(controlu_1_jump), .Q(register_1_q), .clk(clock_1_out));  // open: clr
  Multiplexer #(.width(16)) multiplexer_1 (
    .in0(multiplexer_2_out), .in1(register_1_q), .out(multiplexer_1_out), .sel(controlu_1_jumpback));  // open: en
  ControlU controlu_1 (
    .A3(ram_1_data_2[29]), .A2(ram_1_data_2[28]), .RegWrite(controlu_1_regwrite), .A1(ram_1_data_2[27]),
    .A0(ram_1_data_2[26]), .AluSrc(controlu_1_alusrc), .MemWrite(controlu_1_memwrite),
    .MemToReq(controlu_1_memtoreq), .MemRead(controlu_1_memread), .Branch(controlu_1_branch),
    .Jump(controlu_1_jump), .RegDst(controlu_1_regdst), .AluOp1(controlu_1_aluop1[0]),
    .AluOp2(controlu_1_aluop1[1]), .AluOp3(controlu_1_aluop1[2]), .AluOp4(controlu_1_aluop1[3]),
    .JumpBack(controlu_1_jumpback));
  Multiplexer #(.width(16)) multiplexer_2 (
    .in0(n16bit_adder_1_sum), .in1(ram_1_data), .out(multiplexer_2_out), .sel(branch_or_jump_out));  // open: en
  Register #(.width(16)) PC (.D(multiplexer_1_out), .Q(PC_q), .clk(clock_1_out));  // open: en, clr
  or branch_or_jump (branch_or_jump_out, controlu_1_jump, and_1_out);
  _16bit_adder u_16bit_adder_1 (.Sum(n16bit_adder_1_sum), .A(16'h4), .B(PC_q));  // open: Cout
  RAM #(.addrWidth(16), .dataWidth(32)) ram_1 (
    .addr(PC_q), .data({ram_1_data_2, ram_1_data}), .clk(clock_1_out));  // open: sel, ld, clr
  Multiplexer #(.width(5)) multiplexer_3 (
    .in0(ram_1_data_2[20:16]), .in1(ram_1_data[15:11]), .out(multiplexer_3_out), .sel(controlu_1_regdst));  // open: en
  and and_1 (and_1_out, or_1_out, controlu_1_branch);
  Clock clock_1 (.out(clock_1_out));
  register_file register_file_1 (
    .ReadAddress1(ram_1_data_2[25:21]), .ReadAddress2(ram_1_data_2[20:16]), .WriteData(multiplexer_5_out),
    .RegWrite(controlu_1_regwrite), .WriteAddress(multiplexer_3_out[3:0]), .R1(register_file_1_r1),
    .R2(register_file_1_r2), .CLOCK(clock_1_out));
  or or_1 (or_1_out, and_2_out, alu_1_out[15]);
  Multiplexer #(.width(16)) multiplexer_4 (
    .in0(register_file_1_r2), .in1(ram_1_data), .out(multiplexer_4_out), .sel(controlu_1_alusrc));  // open: en
  ALU alu_1 (
    .A(register_file_1_r1), .B(multiplexer_4_out), .shamt(ram_1_data[10:6]), .OP({2'b00, controlu_1_aluop1}),
    .OUT(alu_1_out), .CLOCK(clock_1_out));  // open: Overflow
  and and_2 (and_2_out, ~alu_1_out[15], ~alu_1_out[14], ~alu_1_out[13], ~alu_1_out[12], ~alu_1_out[11], ~alu_1_out[10], ~alu_1_out[9], ~alu_1_out[8], ~alu_1_out[6], ~alu_1_out[5], ~alu_1_out[4], ~alu_1_out[3], ~alu_1_out[2], ~alu_1_out[1], ~alu_1_out[0], ~alu_1_out[7]);  // AND_Gate
  RAM #(.addrWidth(16), .dataWidth(16), .bus("separate")) ram_2 (
    .addr(alu_1_out), .din(register_file_1_r2), .data(ram_2_data), .str(controlu_1_memwrite),
    .clk(clock_1_out), .ld(controlu_1_memread));  // open: sel, clr
  Multiplexer #(.width(16)) multiplexer_5 (
    .in0(alu_1_out), .in1(ram_2_data), .out(multiplexer_5_out), .sel(controlu_1_memtoreq));  // open: en
endmodule

module ALU (
  input  [15:0] A,
  input  [15:0] B,
  input  [4:0] shamt,
  input  [5:0] OP,
  input  CLOCK,
  output [15:0] OUT,
  output Overflow
);

  wire and_2_out, comparator_1_lt, n16bit_adder_1_cout, n16bit_adder_2_cout, not_1_out, not_2_out, not_3_out;
  wire [15:0] and_1_out, bit_extender_1_out, HIGH_q, LOW_q, multiplexer_1_out, multiplexer_2_out,
       multiplexer_3_out, multiplexer_4_out, multiplexer_5_out, multiplexer_6_out, multiplexer_7_out,
       multiplexer_8_out, multiplier_1_cout, multiplier_1_out, n16bit_adder_1_sum, n16bit_adder_2_sum,
       or_2_out, shifter_1_out, subtractor_1_out;

  or or_1 (Overflow, n16bit_adder_1_cout, n16bit_adder_2_cout);
  _16bit_adder u_16bit_adder_1 (.Sum(n16bit_adder_1_sum), .A(A), .B(B), .Cout(n16bit_adder_1_cout));
  Subtractor #(.width(16)) subtractor_1 (.a(A), .b(B), .out(subtractor_1_out));  // open: bin, bout
  Multiplier #(.width(16)) multiplier_1 (.a(A), .b(B), .out(multiplier_1_out), .cout(multiplier_1_cout));  // open: cin
  assign and_1_out = A & B;  // AND_Gate and_1, 16 bits wide
  assign or_2_out = A | B;  // OR_Gate or_2, 16 bits wide
  _16bit_adder u_16bit_adder_2 (.Sum(n16bit_adder_2_sum), .A(A), .B(B), .Cout(n16bit_adder_2_cout));
  Shifter #(.width(16)) shifter_1 (.in(A), .\dist (shamt[3:0]), .out(shifter_1_out));
  Comparator #(.width(16)) comparator_1 (.a(A), .b(B), .lt(comparator_1_lt));  // open: gt, eq
  assign bit_extender_1_out = {{15{1'b0}}, comparator_1_lt};  // Bit_Extender bit_extender_1
  Register #(.width(16)) LOW (.D(multiplier_1_out), .en(and_2_out), .Q(LOW_q), .clk(CLOCK));  // open: clr
  Register #(.width(16)) HIGH (.D(multiplier_1_cout), .en(and_2_out), .Q(HIGH_q), .clk(CLOCK));  // open: clr
  and and_2 (and_2_out, not_1_out, not_2_out, OP[1], not_3_out);
  Multiplexer #(.width(16)) multiplexer_1 (
    .in0(n16bit_adder_1_sum), .in1(subtractor_1_out), .out(multiplexer_1_out), .sel(OP[0]));  // open: en
  Multiplexer #(.width(16)) multiplexer_2 (.in1(and_1_out), .out(multiplexer_2_out), .sel(OP[0]));  // open: in0, en
  Multiplexer #(.width(16)) multiplexer_3 (
    .in0(or_2_out), .in1(n16bit_adder_2_sum), .out(multiplexer_3_out), .sel(OP[0]));  // open: en
  Multiplexer #(.width(16)) multiplexer_4 (
    .in0(shifter_1_out), .in1(bit_extender_1_out), .out(multiplexer_4_out), .sel(OP[0]));  // open: en
  Multiplexer #(.width(16)) multiplexer_5 (
    .in0(HIGH_q), .in1(LOW_q), .out(multiplexer_5_out), .sel(OP[0]));  // open: en
  not not_1 (not_1_out, OP[3]);
  not not_2 (not_2_out, OP[2]);
  not not_3 (not_3_out, OP[0]);
  Multiplexer #(.width(16)) multiplexer_6 (
    .in0(multiplexer_1_out), .in1(multiplexer_2_out), .out(multiplexer_6_out), .sel(OP[1]));  // open: en
  Multiplexer #(.width(16)) multiplexer_7 (
    .in0(multiplexer_6_out), .in1(multiplexer_8_out), .out(multiplexer_7_out), .sel(OP[2]));  // open: en
  Multiplexer #(.width(16)) multiplexer_8 (
    .in0(multiplexer_3_out), .in1(multiplexer_4_out), .out(multiplexer_8_out), .sel(OP[1]));  // open: en
  Multiplexer #(.width(16)) multiplexer_9 (
    .in0(multiplexer_7_out), .in1(multiplexer_5_out), .out(OUT), .sel(OP[3]));  // open: en
endmodule

module full_adder (
  input  A,
  input  B,
  input  Cin,
  output Sum,
  output Cout
);

  wire and_1_out, and_2_out, xor_1_out;

  xor xor_1 (xor_1_out, A, B);
  xor xor_2 (Sum, xor_1_out, Cin);
  and and_1 (and_1_out, Cin, xor_1_out);
  and and_2 (and_2_out, B, A);
  or or_1 (Cout, and_1_out, and_2_out);
endmodule

module register_file (
  input  [4:0] ReadAddress1,
  input  [4:0] ReadAddress2,
  input  [15:0] WriteData,
  input  RegWrite,
  input  [3:0] WriteAddress,
  input  CLOCK,
  output [15:0] R1,
  output [15:0] R2
);

  wire and_1_out, and_2_out, demultiplexer_1_out1, demultiplexer_1_out2, demultiplexer_1_out3,
       demultiplexer_1_out4, demultiplexer_1_out5, demultiplexer_1_out6, demultiplexer_1_out7,
       demultiplexer_1_out8, demultiplexer_1_out9, demultiplexer_1_out10, demultiplexer_1_out11,
       demultiplexer_1_out12, demultiplexer_1_out13, demultiplexer_1_out14, demultiplexer_1_out15, not_1_out;
  wire [15:0] _0_q, _1_q, _2_q, _3_q, _4_q, _5_q, _6_q, _7_q, _8_q, _9_q, _10_q, _11_q, _12_q, _13_q, _14_q,
       _15_q;

  and and_1 (and_1_out, CLOCK, not_1_out);
  not not_1 (not_1_out, CLOCK);
  Demultiplexer #(.select(4)) demultiplexer_1 (
    .out1(demultiplexer_1_out1), .out2(demultiplexer_1_out2), .out3(demultiplexer_1_out3),
    .out4(demultiplexer_1_out4), .out5(demultiplexer_1_out5), .out6(demultiplexer_1_out6),
    .out7(demultiplexer_1_out7), .out8(demultiplexer_1_out8), .out9(demultiplexer_1_out9),
    .out10(demultiplexer_1_out10), .out11(demultiplexer_1_out11), .out12(demultiplexer_1_out12),
    .out13(demultiplexer_1_out13), .out14(demultiplexer_1_out14), .out15(demultiplexer_1_out15),
    .in(and_2_out), .sel(WriteAddress));  // open: out0, en
  and and_2 (and_2_out, RegWrite, and_1_out);
  Register #(.width(16)) _0 (.Q(_0_q));  // open: D, en, clk, clr
  Register #(.width(16)) _4 (.D(WriteData), .Q(_4_q), .clk(demultiplexer_1_out4));  // open: en, clr
  Register #(.width(16)) _8 (.D(WriteData), .Q(_8_q), .clk(demultiplexer_1_out8));  // open: en, clr
  Register #(.width(16)) _12 (.D(WriteData), .Q(_12_q), .clk(demultiplexer_1_out12));  // open: en, clr
  Register #(.width(16)) _1 (.D(WriteData), .Q(_1_q), .clk(demultiplexer_1_out1));  // open: en, clr
  Register #(.width(16)) _5 (.D(WriteData), .Q(_5_q), .clk(demultiplexer_1_out5));  // open: en, clr
  Register #(.width(16)) _9 (.D(WriteData), .Q(_9_q), .clk(demultiplexer_1_out9));  // open: en, clr
  Register #(.width(16)) _13 (.D(WriteData), .Q(_13_q), .clk(demultiplexer_1_out13));  // open: en, clr
  Register #(.width(16)) _2 (.D(WriteData), .Q(_2_q), .clk(demultiplexer_1_out2));  // open: en, clr
  Register #(.width(16)) _6 (.D(WriteData), .Q(_6_q), .clk(demultiplexer_1_out6));  // open: en, clr
  Register #(.width(16)) _10 (.D(WriteData), .Q(_10_q), .clk(demultiplexer_1_out10));  // open: en, clr
  Register #(.width(16)) _14 (.D(WriteData), .Q(_14_q), .clk(demultiplexer_1_out14));  // open: en, clr
  Register #(.width(16)) _3 (.D(WriteData), .Q(_3_q), .clk(demultiplexer_1_out3));  // open: en, clr
  Register #(.width(16)) _7 (.D(WriteData), .Q(_7_q), .clk(demultiplexer_1_out7));  // open: en, clr
  Register #(.width(16)) _11 (.D(WriteData), .Q(_11_q), .clk(demultiplexer_1_out11));  // open: en, clr
  Register #(.width(16)) _15 (.D(WriteData), .Q(_15_q), .clk(demultiplexer_1_out15));  // open: en, clr
  Multiplexer #(.select(4), .width(16)) multiplexer_1 (
    .in0(_0_q), .in1(_1_q), .in2(_2_q), .in3(_3_q), .in4(_4_q), .in5(_5_q), .in6(_6_q), .in7(_7_q),
    .in8(_8_q), .in9(_9_q), .in10(_10_q), .in11(_11_q), .in12(_12_q), .in13(_13_q), .in14(_14_q),
    .in15(_15_q), .out(R1), .sel(ReadAddress1[3:0]));  // open: en
  Multiplexer #(.select(4), .width(16)) multiplexer_2 (
    .in0(_0_q), .in1(_1_q), .in2(_2_q), .in3(_3_q), .in4(_4_q), .in5(_5_q), .in6(_6_q), .in7(_7_q),
    .in8(_8_q), .in9(_9_q), .in10(_10_q), .in11(_11_q), .in12(_12_q), .in13(_13_q), .in14(_14_q),
    .in15(_15_q), .out(R2), .sel(ReadAddress2[3:0]));  // open: en
endmodule

module _16bit_adder (
  input  [15:0] A,
  input  [15:0] B,
  output [15:0] Sum,
  output Cout
);

  wire _0_cout, _1_cout, _2_cout, _3_cout, _4_cout, _5_cout, _6_cout, _7_cout, _8_cout, _9_cout, _10_cout,
       _11_cout, _12_cout, _13_cout, _14_cout;

  full_adder _0 (.A(A[0]), .B(B[0]), .Cin(1'b0), .Sum(Sum[0]), .Cout(_0_cout));
  full_adder _4 (.A(A[4]), .B(B[4]), .Cin(_3_cout), .Sum(Sum[4]), .Cout(_4_cout));
  full_adder _8 (.A(A[8]), .B(B[8]), .Cin(_7_cout), .Sum(Sum[8]), .Cout(_8_cout));
  full_adder _12 (.A(A[12]), .B(B[12]), .Cin(_11_cout), .Sum(Sum[12]), .Cout(_12_cout));
  full_adder _1 (.A(A[1]), .B(B[1]), .Cin(_0_cout), .Sum(Sum[1]), .Cout(_1_cout));
  full_adder _5 (.A(A[5]), .B(B[5]), .Cin(_4_cout), .Sum(Sum[5]), .Cout(_5_cout));
  full_adder _9 (.A(A[9]), .B(B[9]), .Cin(_8_cout), .Sum(Sum[9]), .Cout(_9_cout));
  full_adder _13 (.A(A[13]), .B(B[13]), .Cin(_12_cout), .Sum(Sum[13]), .Cout(_13_cout));
  full_adder _2 (.A(A[2]), .B(B[2]), .Cin(_1_cout), .Sum(Sum[2]), .Cout(_2_cout));
  full_adder _6 (.A(A[6]), .B(B[6]), .Cin(_5_cout), .Sum(Sum[6]), .Cout(_6_cout));
  full_adder _10 (.A(A[10]), .B(B[10]), .Cin(_9_cout), .Sum(Sum[10]), .Cout(_10_cout));
  full_adder _14 (.A(A[14]), .B(B[14]), .Cin(_13_cout), .Sum(Sum[14]), .Cout(_14_cout));
  full_adder _3 (.A(A[3]), .B(B[3]), .Cin(_2_cout), .Sum(Sum[3]), .Cout(_3_cout));
  full_adder _7 (.A(A[7]), .B(B[7]), .Cin(_6_cout), .Sum(Sum[7]), .Cout(_7_cout));
  full_adder _11 (.A(A[11]), .B(B[11]), .Cin(_10_cout), .Sum(Sum[11]), .Cout(_11_cout));
  full_adder _15 (.A(A[15]), .B(B[15]), .Cin(_14_cout), .Sum(Sum[15]), .Cout(Cout));
endmodule

module ControlU (
  input  A3,
  input  A2,
  input  A1,
  input  A0,
  output RegWrite,
  output AluSrc,
  output MemWrite,
  output MemToReq,
  output MemRead,
  output Branch,
  output Jump,
  output RegDst,
  output AluOp1,
  output AluOp2,
  output AluOp3,
  output AluOp4,
  output JumpBack
);

  wire and_1_out, and_2_out, and_3_out, and_4_out, and_6_out, and_7_out, and_8_out, and_9_out, and_10_out,
       and_11_out, and_12_out, and_13_out, and_14_out, and_16_out, and_17_out, and_19_out, and_20_out,
       not_1_out, not_2_out, not_3_out, not_4_out, not_5_out, not_6_out, not_7_out, not_8_out, not_9_out,
       not_10_out, not_11_out, not_12_out, not_13_out, not_14_out, not_15_out, not_16_out, not_17_out,
       not_18_out, not_19_out, not_20_out, not_21_out, not_22_out, not_23_out, not_24_out, not_25_out,
       not_26_out, not_27_out, not_28_out, not_29_out, not_30_out, not_31_out, not_32_out, not_33_out,
       not_34_out;

  not not_1 (not_1_out, A2);
  and and_1 (and_1_out, not_1_out, not_2_out);
  not not_2 (not_2_out, A1);
  not not_3 (not_3_out, A3);
  and and_2 (and_2_out, not_3_out, A0);
  not not_4 (not_4_out, A3);
  and and_3 (and_3_out, not_4_out, A2);
  not not_5 (not_5_out, A2);
  and and_4 (and_4_out, A3, not_5_out, not_6_out);
  not not_6 (not_6_out, A0);
  not not_7 (not_7_out, A3);
  not not_8 (not_8_out, A1);
  not not_9 (not_9_out, A2);
  not not_10 (not_10_out, A2);
  not not_11 (not_11_out, A2);
  not not_12 (not_12_out, A0);
  not not_13 (not_13_out, A2);
  not not_14 (not_14_out, A0);
  and and_5 (Branch, A3, A2, not_15_out);
  not not_15 (not_15_out, A1);
  not not_16 (not_16_out, A0);
  not not_17 (not_17_out, A3);
  and and_6 (and_6_out, not_17_out, not_18_out);
  not not_18 (not_18_out, A2);
  not not_19 (not_19_out, A3);
  not not_20 (not_20_out, A1);
  and and_7 (and_7_out, not_19_out, not_20_out, not_21_out);
  not not_21 (not_21_out, A0);
  not not_22 (not_22_out, A2);
  and and_8 (and_8_out, not_22_out, not_23_out);
  not not_23 (not_23_out, A1);
  not not_24 (not_24_out, A3);
  and and_9 (and_9_out, not_24_out, A1, A0);
  not not_25 (not_25_out, A1);
  and and_10 (and_10_out, A3, not_25_out, A0);
  not not_26 (not_26_out, A3);
  and and_11 (and_11_out, not_26_out, A0);
  not not_27 (not_27_out, A2);
  and and_12 (and_12_out, not_27_out, A0);
  not not_28 (not_28_out, A2);
  and and_13 (and_13_out, A3, not_28_out, A1);
  and and_14 (and_14_out, A3, A2, not_29_out);
  not not_29 (not_29_out, A1);
  not not_30 (not_30_out, A3);
  and and_15 (AluOp2, not_30_out, A1);
  not not_31 (not_31_out, A3);
  and and_16 (and_16_out, not_31_out, A2);
  not not_32 (not_32_out, A2);
  and and_17 (and_17_out, A3, not_32_out, A1);
  and and_18 (AluOp4, A3, not_33_out, not_34_out);
  not not_33 (not_33_out, A2);
  not not_34 (not_34_out, A1);
  or or_1 (RegWrite, and_1_out, and_2_out, and_3_out, and_4_out);
  and and_19 (and_19_out, not_7_out, A2, not_8_out, A0);
  or or_2 (AluSrc, and_19_out, and_20_out);
  and and_20 (and_20_out, A3, not_9_out, A1);
  and and_21 (MemWrite, A3, not_10_out, A1, A0);
  and and_22 (MemToReq, A3, not_11_out, A1, not_12_out);
  and and_23 (MemRead, A3, not_13_out, A1, not_14_out);
  and and_24 (Jump, A3, A2, A1, not_16_out);
  or or_3 (RegDst, and_6_out, and_7_out, and_8_out, and_9_out, and_10_out);
  or or_4 (AluOp1, and_11_out, and_12_out, and_13_out, and_14_out);
  or or_5 (AluOp3, and_16_out, and_17_out);
  and and_25 (JumpBack, A0, A1, A2, A3);
endmodule

module merger (
  input  [27:0] _28_in,
  input  [15:0] _32_in,
  output [31:0] out
);

  wire [27:16] undriven;

  // Pins of 16 and 32 bits meet at {out[31:28], undriven, _32_in}

  assign out[27:0] = _28_in;
endmodule
