// Logisim project alu.circ as structural Verilog: 3 circuits, main circuit main
module main (
  input  [15:0] in_1,
  input  [15:0] in_2,
  input  [3:0] in_3,
  input  [5:0] in_4,
  output [15:0] out_5,
  output Overflow
);

  wire and_2_out, clock_1_out, comparator_1_lt, n16bit_adder_1_cout, n16bit_adder_2_cout, not_1_out,
       not_2_out, not_3_out;
  wire [15:0] and_1_out, bit_extender_1_out, HIGH_q, LOW_q, multiplexer_1_out, multiplexer_2_out,
       multiplexer_3_out, multiplexer_4_out, multiplexer_5_out, multiplexer_6_out, multiplexer_7_out,
       multiplexer_8_out, multiplier_1_cout, multiplier_1_out, n16bit_adder_1_sum, n16bit_adder_2_sum,
       or_2_out, shifter_1_out, subtractor_1_out;

  or or_1 (Overflow, n16bit_adder_1_cout, n16bit_adder_2_cout);
  _16bit_adder u_16bit_adder_1 (.Sum(n16bit_adder_1_sum), .A(in_1), .B(in_2), .Cout(n16bit_adder_1_cout));
  Subtractor #(.width(16)) subtractor_1 (.a(in_1), .b(in_2), .out(subtractor_1_out));  // open: bin, bout
  Multiplier #(.width(16)) multiplier_1 (
    .a(in_1), .b(in_2), .out(multiplier_1_out), .cout(multiplier_1_cout));  // open: cin
  assign and_1_out = in_1 & in_2;  // AND_Gate and_1, 16 bits wide
  assign or_2_out = in_1 | in_2;  // OR_Gate or_2, 16 bits wide
  _16bit_adder u_16bit_adder_2 (.Sum(n16bit_adder_2_sum), .A(in_1), .B(in_2), .Cout(n16bit_adder_2_cout));
  Shifter #(.width(16)) shifter_1 (.in(in_1), .\dist (in_3), .out(shifter_1_out));
  Comparator #(.width(16)) comparator_1 (.a(in_1), .b(in_2), .lt(comparator_1_lt));  // open: gt, eq
  assign bit_extender_1_out = {{15{1'b0}}, comparator_1_lt};  // Bit_Extender bit_extender_1
  Register #(.width(16)) LOW (.D(multiplier_1_out), .en(and_2_out), .Q(LOW_q), .clk(clock_1_out));  // open: clr
  Register #(.width(16)) HIGH (.D(multiplier_1_cout), .en(and_2_out), .Q(HIGH_q), .clk(clock_1_out));  // open: clr
  Clock clock_1 (.out(clock_1_out));
  and and_2 (and_2_out, not_1_out, not_2_out, in_4[1], not_3_out);
  Multiplexer #(.width(16)) multiplexer_1 (
    .in0(n16bit_adder_1_sum), .in1(subtractor_1_out), .out(multiplexer_1_out), .sel(in_4[0]));  // open: en
  Multiplexer #(.width(16)) multiplexer_2 (.in1(and_1_out), .out(multiplexer_2_out), .sel(in_4[0]));  // open: in0, en
  Multiplexer #(.width(16)) multiplexer_3 (
    .in0(or_2_out), .in1(n16bit_adder_2_sum), .out(multiplexer_3_out), .sel(in_4[0]));  // open: en
  Multiplexer #(.width(16)) multiplexer_4 (
    .in0(shifter_1_out), .in1(bit_extender_1_out), .out(multiplexer_4_out), .sel(in_4[0]));  // open: en
  Multiplexer #(.width(16)) multiplexer_5 (
    .in0(HIGH_q), .in1(LOW_q), .out(multiplexer_5_out), .sel(in_4[0]));  // open: en
  not not_1 (not_1_out, in_4[3]);
  not not_2 (not_2_out, in_4[2]);
  not not_3 (not_3_out, in_4[0]);
  Multiplexer #(.width(16)) multiplexer_6 (
    .in0(multiplexer_1_out), .in1(multiplexer_2_out), .out(multiplexer_6_out), .sel(in_4[1]));  // open: en
  Multiplexer #(.width(16)) multiplexer_7 (
    .in0(multiplexer_6_out), .in1(multiplexer_8_out), .out(multiplexer_7_out), .sel(in_4[2]));  // open: en
  Multiplexer #(.width(16)) multiplexer_8 (
    .in0(multiplexer_3_out), .in1(multiplexer_4_out), .out(multiplexer_8_out), .sel(in_4[1]));  // open: en
  Multiplexer #(.width(16)) multiplexer_9 (
    .in0(multiplexer_7_out), .in1(multiplexer_5_out), .out(out_5), .sel(in_4[3]));  // open: en
endmodule

module full_adder (
  input  A,
  input  B,
  input  Cin,
  output Sum,
  output Cout
);

  wire and_1_out, and_2_out, xor_1_out;

  xor xor_1 (xor_1_out, A, B);
  xor xor_2 (Sum, xor_1_out, Cin);
  and and_1 (and_1_out, Cin, xor_1_out);
  and and_2 (and_2_out, B, A);
  or or_1 (Cout, and_1_out, and_2_out);
endmodule

module _16bit_adder (
  input  [15:0] A,
  input  [15:0] B,
  output [15:0] Sum,
  output Cout
);

  wire _0_cout, _1_cout, _2_cout, _3_cout, _4_cout, _5_cout, _6_cout, _7_cout, _8_cout, _9_cout, _10_cout,
       _11_cout, _12_cout, _13_cout, _14_cout;

  full_adder _0 (.A(A[0]), .B(B[0]), .Cin(1'b0), .Sum(Sum[0]), .Cout(_0_cout));
  full_adder _4 (.A(A[4]), .B(B[4]), .Cin(_3_cout), .Sum(Sum[4]), .Cout(_4_cout));
  full_adder _8 (.A(A[8]), .B(B[8]), .Cin(_7_cout), .Sum(Sum[8]), .Cout(_8_cout));
  full_adder _12 (.A(A[12]), .B(B[12]), .Cin(_11_cout), .Sum(Sum[12]), .Cout(_12_cout));
  full_adder _1 (.A(A[1]), .B(B[1]), .Cin(_0_cout), .Sum(Sum[1]), .Cout(_1_cout));
  full_adder _5 (.A(A[5]), .B(B[5]), .Cin(_4_cout), .Sum(Sum[5]), .Cout(_5_cout));
  full_adder _9 (.A(A[9]), .B(B[9]), .Cin(_8_cout), .Sum(Sum[9]), .Cout(_9_cout));
  full_adder _13 (.A(A[13]), .B(B[13]), .Cin(_12_cout), .Sum(Sum[13]), .Cout(_13_cout));
  full_adder _2 (.A(A[2]), .B(B[2]), .Cin(_1_cout), .Sum(Sum[2]), .Cout(_2_cout));
  full_adder _6 (.A(A[6]), .B(B[6]), .Cin(_5_cout), .Sum(Sum[6]), .Cout(_6_cout));
  full_adder _10 (.A(A[10]), .B(B[10]), .Cin(_9_cout), .Sum(Sum[10]), .Cout(_10_cout));
  full_adder _14 (.A(A[14]), .B(B[14]), .Cin(_13_cout), .Sum(Sum[14]), .Cout(_14_cout));
  full_adder _3 (.A(A[3]), .B(B[3]), .Cin(_2_cout), .Sum(Sum[3]), .Cout(_3_cout));
  full_adder _7 (.A(A[7]), .B(B[7]), .Cin(_6_cout), .Sum(Sum[7]), .Cout(_7_cout));
  full_adder _11 (.A(A[11]), .B(B[11]), .Cin(_10_cout), .Sum(Sum[11]), .Cout(_11_cout));
  full_adder _15 (.A(A[15]), .B(B[15]), .Cin(_14_cout), .Sum(Sum[15]), .Cout(Cout));
endmodule
