// Logisim project register.circ as structural Verilog: 1 circuit, main circuit main
module main (
  input  [4:0] ReadAddress1,
  input  [4:0] ReadAddress2,
  input  [15:0] WriteData,
  input  RegWrite,
  input  [3:0] WriteAddress,
  output [15:0] R1,
  output [15:0] R2
);

  wire demultiplexer_1_out0, demultiplexer_1_out1, demultiplexer_1_out2, demultiplexer_1_out3,
       demultiplexer_1_out4, demultiplexer_1_out5, demultiplexer_1_out6, demultiplexer_1_out7,
       demultiplexer_1_out8, demultiplexer_1_out9, demultiplexer_1_out10, demultiplexer_1_out11,
       demultiplexer_1_out12, demultiplexer_1_out13, demultiplexer_1_out14, demultiplexer_1_out15;
  wire [15:0] _0_q, _1_q, _2_q, _3_q, _4_q, _5_q, _6_q, _7_q, _8_q, _9_q, _10_q, _11_q, _12_q, _13_q, _14_q,
       _15_q;

  Demultiplexer #(.select(4)) demultiplexer_1 (
    .out0(demultiplexer_1_out0), .out1(demultiplexer_1_out1), .out2(demultiplexer_1_out2),
    .out3(demultiplexer_1_out3), .out4(demultiplexer_1_out4), .out5(demultiplexer_1_out5),
    .out6(demultiplexer_1_out6), .out7(demultiplexer_1_out7), .out8(demultiplexer_1_out8),
    .out9(demultiplexer_1_out9), .out10(demultiplexer_1_out10), .out11(demultiplexer_1_out11),
    .out12(demultiplexer_1_out12), .out13(demultiplexer_1_out13), .out14(demultiplexer_1_out14),
    .out15(demultiplexer_1_out15), .in(RegWrite), .sel(WriteAddress));  // open: en
  Register #(.width(16), .trigger("high")) _0 (.D(WriteData), .Q(_0_q), .clk(demultiplexer_1_out0));  // open: en, clr
  Register #(.width(16), .trigger("high")) _4 (.D(WriteData), .Q(_4_q), .clk(demultiplexer_1_out4));  // open: en, clr
  Register #(.width(16), .trigger("high")) _8 (.D(WriteData), .Q(_8_q), .clk(demultiplexer_1_out8));  // open: en, clr
  Register #(.width(16), .trigger("high")) _12 (
    .D(WriteData), .Q(_12_q), .clk(demultiplexer_1_out12));  // open: en, clr
  Register #(.width(16), .trigger("high")) _1 (.D(WriteData), .Q(_1_q), .clk(demultiplexer_1_out1));  // open: en, clr
  Register #(.width(16), .trigger("high")) _5 (.D(WriteData), .Q(_5_q), .clk(demultiplexer_1_out5));  // open: en, clr
  Register #(.width(16), .trigger("high")) _9 (.D(WriteData), .Q(_9_q), .clk(demultiplexer_1_out9));  // open: en, clr
  Register #(.width(16), .trigger("high")) _13 (
    .D(WriteData), .Q(_13_q), .clk(demultiplexer_1_out13));  // open: en, clr
  Register #(.width(16), .trigger("high")) _2 (.D(WriteData), .Q(_2_q), .clk(demultiplexer_1_out2));  // open: en, clr
  Register #(.width(16), .trigger("high")) _6 (.D(WriteData), .Q(_6_q), .clk(demultiplexer_1_out6));  // open: en, clr
  Register #(.width(16), .trigger("high")) _10 (
    .D(WriteData), .Q(_10_q), .clk(demultiplexer_1_out10));  // open: en, clr
  Register #(.width(16), .trigger("high")) _14 (
    .D(WriteData), .Q(_14_q), .clk(demultiplexer_1_out14));  // open: en, clr
  Register #(.width(16), .trigger("high")) _3 (.D(WriteData), .Q(_3_q), .clk(demultiplexer_1_out3));  // open: en, clr
  Register #(.width(16), .trigger("high")) _7 (.D(WriteData), .Q(_7_q), .clk(demultiplexer_1_out7));  // open: en, clr
  Register #(.width(16), .trigger("high")) _11 (
    .D(WriteData), .Q(_11_q), .clk(demultiplexer_1_out11));  // open: en, clr
  Register #(.width(16), .trigger("high")) _15 (
    .D(WriteData), .Q(_15_q), .clk(demultiplexer_1_out15));  // open: en, clr
  Multiplexer #(.select(4), .width(16)) multiplexer_1 (
    .in0(_0_q), .in1(_1_q), .in2(_2_q), .in3(_3_q), .in4(_4_q), .in5(_5_q), .in6(_6_q), .in7(_7_q),
    .in8(_8_q), .in9(_9_q), .in10(_10_q), .in11(_11_q), .in12(_12_q), .in13(_13_q), .in14(_14_q),
    .in15(_15_q), .out(R1), .sel(ReadAddress1[3:0]));  // open: en
  Multiplexer #(.select(4), .width(16)) multiplexer_2 (
    .in0(_0_q), .in1(_1_q), .in2(_2_q), .in3(_3_q), .in4(_4_q), .in5(_5_q), .in6(_6_q), .in7(_7_q),
    .in8(_8_q), .in9(_9_q), .in10(_10_q), .in11(_11_q), .in12(_12_q), .in13(_13_q), .in14(_14_q),
    .in15(_15_q), .out(R2), .sel(ReadAddress2[3:0]));  // open: en
endmodule
